# Fritzing sketch USBMIDIMixer (saved by Fritzing 0.9.4)
perfboards: 1

parts:
  S1 = Round Pushbutton
  Mcrctrlr = Adafruit QT Py [part_number="QT Py"]
  VR4 = Slide Potentiometer [maximum_resistance=10kΩ]
  VR5 = Slide Potentiometer [maximum_resistance=10kΩ]
  VR2 = Slide Potentiometer [maximum_resistance=10kΩ]
  VR1 = Slide Potentiometer [maximum_resistance=10kΩ]
  R1 = Resistor [tolerance=±5% resistance=1k package=THT]
  VR3 = Slide Potentiometer [maximum_resistance=10kΩ]
  R3 = Resistor [tolerance=±5% resistance=10k package=THT]
  S2 = Round Pushbutton
  R2 = Resistor [tolerance=±5% resistance=5k package=THT]
  S3 = Round Pushbutton
  S4 = Round Pushbutton
  R4 = Resistor [tolerance=±5% resistance=10k package=THT]
  R6 = Resistor [tolerance=±5% resistance=1k package=THT]
  S5 = Round Pushbutton
  R9 = Resistor [tolerance=±5% resistance=10k package=THT]
  LED1 = LED - 5mm [color="Red (633nm)" package="5 mm [THT]"]
  LED2 = LED - 5mm [color="Red (633nm)" package="5 mm [THT]"]
  LED3 = LED - 5mm [color="Red (633nm)" package="5 mm [THT]"]
  LED4 = LED - 5mm [color="Red (633nm)" package="5 mm [THT]"]
  LED5 = LED - 5mm [color="Red (633nm)" package="5 mm [THT]"]
  R10 = Resistor [tolerance=±5% resistance=1k package=THT]
  R11 = Resistor [tolerance=±5% resistance=1k package=THT]
  R12 = Resistor [tolerance=±5% resistance=1k package=THT]
  R5 = Resistor [tolerance=±5% resistance=5k package=THT]

nets:
  N1: S1.leg0, R1.Pin_0
  3.3V: S1.leg1, Mcrctrlr.3.3V, VR4.leg2, VR5.leg2, VR2.leg2, VR1.leg2, VR3.leg2, S2.leg1, S3.leg1, S4.leg1, S5.leg1
  GND: Mcrctrlr.GND, VR4.leg1, VR5.leg1, VR2.leg1, VR1.leg1, VR3.leg1, R3.Pin_1, R4.Pin_1, R9.Pin_1
  N2: Mcrctrlr.SDA, R10.Pin_1
  N3: Mcrctrlr.SCL, R11.Pin_1
  N4: Mcrctrlr.A0, VR2.wiper
  N5: Mcrctrlr.A1, VR3.wiper
  N6: Mcrctrlr.A2, VR4.wiper
  N7: Mcrctrlr.A3, VR5.wiper
  N8: Mcrctrlr.TX_A6, R12.Pin_1
  N9: Mcrctrlr.RX_A7, S5.leg0, R9.Pin_0
  N10: Mcrctrlr.SCK, R4.Pin_0, R6.Pin_1, R5.Pin_1
  N11: Mcrctrlr.MISO, R1.Pin_1, R3.Pin_0, R2.Pin_1
  N12: Mcrctrlr.MOSI, VR1.wiper
  N13: S2.leg0, R2.Pin_0
  N14: S3.leg0, R6.Pin_0
  N15: S4.leg0, R5.Pin_0
  N16: LED1.cathode, LED3.anode, LED4.anode, LED5.cathode, R11.Pin_0
  N17: LED1.anode, LED2.anode, LED3.cathode, R10.Pin_0
  N18: LED2.cathode, LED4.cathode, LED5.anode, R12.Pin_0

custom parts:
  Adafruit QT Py: What a cutie pie! Or is it... a QT Py? This diminutive dev board comes with our favorite lil chip, the SAMD21 (as made famous in our GEMMA M0 and Trinket M0 boards). This time it comes with our favorite connector - the STEMMA QT, a chainable I2C port that can be used with any of our STEMMA QT sensors and accessories. OLEDs! Inertial Measurment Units! Sensors a-plenty. All plug-and-play thanks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
